// Logisim project Lab7.circ as structural Verilog: 2 circuits, main circuit subcircuit
module subcircuit (
  input  A,
  input  B,
  input  CLK,
  output Q
);

  wire and_1_out, and_2_out, not_1_out;

  not not_1 (not_1_out, B);
  and and_1 (and_1_out, A, B);
  and and_2 (and_2_out, A, not_1_out);
  J_K_Flip_Flop j_k_ff_1 (.J(and_1_out), .clk(CLK), .K(and_2_out), .Q(Q));  // open: Qn, preset, en, reset
endmodule

module main (
  input  A,
  input  [7:0] B,
  output [7:0] Cout
);

  wire CLK_out;

  Clock CLK (.out(CLK_out));
  subcircuit subcircuit_1 (.A(A), .B(B[0]), .CLK(CLK_out), .Q(Cout[0]));
  subcircuit subcircuit_2 (.A(A), .B(B[1]), .CLK(CLK_out), .Q(Cout[1]));
  subcircuit subcircuit_3 (.A(A), .B(B[2]), .CLK(CLK_out), .Q(Cout[2]));
  subcircuit subcircuit_4 (.A(A), .B(B[4]), .CLK(CLK_out), .Q(Cout[4]));
  subcircuit subcircuit_5 (.A(A), .B(B[3]), .CLK(CLK_out), .Q(Cout[3]));
  subcircuit subcircuit_6 (.A(A), .B(B[5]), .CLK(CLK_out), .Q(Cout[5]));
  subcircuit subcircuit_7 (.A(A), .B(B[6]), .CLK(CLK_out), .Q(Cout[6]));
  subcircuit subcircuit_8 (.A(A), .B(B[7]), .CLK(CLK_out), .Q(Cout[7]));
endmodule
